# Fritzing sketch breadboard (saved by Fritzing 0.9.0b)
breadboards: 1

parts:
  Solar_Cell1 = 5V 100mA Polycrystalline PET Solar Cell [part_number=IM130407002]
  YX2 = YX8018 solar LED driver [part_number=YX8018 package=TO-94]
  LED7 = smd LED [color="Red (633nm)" package="1206 [SMD]"]
  LED8 = smd LED [color="Red (633nm)" package="1206 [SMD]"]
  LED9 = smd LED [color="Red (633nm)" package="1206 [SMD]"]
  BAT2 = Battery Holders [package=battery-aa-kit]
  S2 = Toggle Switch [package=THT]
  L1 = Inductor [package="0805 [SMD]"]

nets:
  N1: Solar_Cell1.GND, YX2.CE
  5V: Solar_Cell1.5V, YX2.VDD, BAT2.-, L1.pin_1
  N2: YX2.LX, LED7.anode, LED8.anode, LED9.anode, L1.pin_0
  N3: YX2.GND, LED7.cathode, LED8.cathode, LED9.cathode, S2.L2
  N4: BAT2.+, S2.COM

custom parts:
  5V 100mA Polycrystalline PET Solar Cell: This is 5V 100mA Polycrystalline PET Solar Cell. It is high quality and exquisite appearance. It is used in all kinds of high-grade electronic products.
  YX8018 solar LED driver: Solar LED driver. During daylight LEDs are switched off and the solar panel recharges the battery. At night the battery powers the LEDs.
